# Fritzing sketch SmartPlant (saved by Fritzing 0.9.3b)
breadboards: 1

parts:
  Componente1 = Arduino Nano (Rev3.0) (ICSP)
  LED1 = LED - 3mm [color="Green (565nm)" package="3 mm [THT]"]
  LED2 = LED - 3mm [color="Red (633nm)" package="3 mm [THT]"]
  R1 = Resistor [tolerance=±5% resistance=220 package="0603 [SMD]"]
  Componente2 = Soil Moisture Sensor
  LCD1 = LCD screen  # not connected
  YwRobot_LCM1602_IIC_VI = IC, DIP package, 8 pins [chip_label="YwRobot LCM1602 IIC VI"]
  J1 = Basic Servo

nets:
  GND: Componente1.GND, LED1.cathode, LED2.cathode, R1.Pin_0, R1.Pin_1, Componente2.GND, J1.gnd
  N1: Componente1.D6, LED1.anode
  N2: Componente1.D7, LED2.anode
  N3: Componente1.D9, J1.pulse
  VCC: Componente1.5V, Componente2.VCC, J1.vcc
  N4: Componente1.A5, YwRobot_LCM1602_IIC_VI.pin5
  N5: Componente1.A4, YwRobot_LCM1602_IIC_VI.pin6
  N6: Componente1.A0, Componente2.SIG
