# Fritzing sketch SmartPlant2-waterpump (saved by Fritzing 0.9.3b)
breadboards: 1

parts:
  Componente1 = Arduino Nano (Rev3.0) (ICSP)
  LED1 = LED - 3mm [color="Green (565nm)" package="3 mm [THT]"]
  LED2 = LED - 3mm [color="Red (633nm)" package="3 mm [THT]"]
  R1 = Resistor [tolerance=±5% resistance=220 package="0603 [SMD]"]
  Componente2 = Soil Moisture Sensor
  LCD1 = LCD screen  # not connected
  YwRobot_LCM1602_IIC_VI = IC, DIP package, 8 pins [chip_label="YwRobot LCM1602 IIC VI"]
  Water_Motor_Pump = DC Motor
  D1 = Zener Diode [part_number=1N4732A breakdown_voltage=3.6V package="Melf DO-213 AB [SMD]"]
  BC547C_Transistor = NPN-Transistor [package="TO92 [THT]"]
  VCC1 = Battery

nets:
  GND: Componente1.GND, LED1.cathode, LED2.cathode, R1.Pin_0, R1.Pin_1, Componente2.GND, Water_Motor_Pump.pin_2, VCC1.-
  N1: Componente1.D6, LED1.anode
  N2: Componente1.D7, LED2.anode
  5V: Componente1.5V, Componente2.VCC
  N3: Componente1.A5, YwRobot_LCM1602_IIC_VI.pin5
  N4: Componente1.A4, YwRobot_LCM1602_IIC_VI.pin6
  N5: Componente1.A3, D1.anode
  N6: Componente1.A0, Componente2.SIG
  N7: Water_Motor_Pump.pin_1, BC547C_Transistor.C
  N8: D1.cathode, BC547C_Transistor.B
  N9: BC547C_Transistor.E, VCC1.+

custom parts:
  Battery: Your standard 2x 18650 battery pack (7,4 Volts)
